# Fritzing sketch arduino fire controller (saved by Fritzing 0.9.3b)

parts:
  Arduino1 = Arduino Mini (Rev5)
  U1 = LIPO-2000mAh [package=lipo-2000]
  R1 = Resistor [tolerance=±5% resistance=1.6k package=THT]
  R2 = Resistor [tolerance=±5% resistance=18k package=THT]
  RE1 = Hexadecimal Rotary Encoder [part_number=APEM-PT65-303 package=THT]
  D2F1 = D2F-FL Omron Snap Action Limit Switch with Level [part_number=Trigger]
  U2 = RELAY [package=relay-t9a-2]
  D1 = Rectifier Diode [package="Melf DO-213 AA [SMD]"]
  Q1 = MOSFET-NCHANNEL [package=to220v]
  Grove1 = Grove OLED 128x96
  C1 = Capacitor [package=cap-pth-small]

nets:
  GND: Arduino1.GND, U1.-, R1.Pin_1, RE1.InputCommon, RE1.InputCommon2, D2F1.COM, Q1.S, Grove1.GND, C1.2
  N1: Arduino1.D2, RE1.Output1Pin
  N2: Arduino1.D3_PWM, RE1.Output2Pin
  N3: Arduino1.D4, D2F1.NO, C1.1
  N4: Arduino1.D5_PWM, Q1.G
  VCC: Arduino1.VCC, Grove1.VCC
  N5: Arduino1.5V, U1.+, R2.Pin_0, U2.COIL1, D1.cathode
  N6: Arduino1.A0, R1.Pin_0, R2.Pin_1
  N7: Arduino1.A4, Grove1.SDA
  N8: Arduino1.A5, Grove1.SCL
  N9: U2.COIL2, D1.anode, Q1.D

custom parts:
  D2F-FL Omron Snap Action Limit Switch with Level: Snap action switch with stainless steel lever.
